// Logisim project ex1.circ as structural Verilog: 5 circuits, main circuit NOR1
module NAND1 (
  input  A,
  input  B,
  output RESULT
);


  // Notes on the sheet:
  //   Fixed I/O
  //   INPUTS
  //   PUT CIRCUITRY HERE
  //   OUTPUTS
  //   Don't touch
endmodule

module NOR1 (
  input  A,
  input  B,
  output RESULT
);


  // Notes on the sheet:
  //   Fixed I/O
  //   INPUTS
  //   PUT CIRCUITRY HERE
  //   OUTPUTS
  //   Don't touch
endmodule

module XOR1 (
  input  A,
  input  B,
  output RESULT
);


  // Notes on the sheet:
  //   Fixed I/O
  //   INPUTS
  //   PUT CIRCUITRY HERE
  //   OUTPUTS
  //   Don't touch
endmodule

module MUX2 (
  input  A,
  input  B,
  input  Sel,
  output RESULT
);


  // Notes on the sheet:
  //   Fixed I/O
  //   INPUTS
  //   PUT CIRCUITRY HERE
  //   Don't touch
  //   OUTPUTS
endmodule

module MUX4 (
  input  A,
  input  B,
  input  C,
  input  D,
  input  Sel1,
  input  Sel2,
  output RESULT
);


  // Notes on the sheet:
  //   Fixed I/O
  //   INPUTS
  //   OUTPUTS
  //   PUT CIRCUITRY HERE
  //   Don't touch
endmodule
