// Logisim project ex1.circ as structural Verilog: 2 circuits, main circuit full_adder
module half_adder (
  input  A,
  input  B,
  output Sum,
  output Cout
);

  xor xor_1 (Sum, A, B);
  and and_1 (Cout, A, B);

  // Notes on the sheet:
  //   Fixed I/O
  //   INPUTS
  //   Don't touch
  //   OUTPUTS
endmodule

module full_adder (
  input  A,
  input  B,
  input  Cin,
  output Sum,
  output Cout
);

  wire and_1_out, and_2_out, xor_1_out;

  xor xor_1 (xor_1_out, A, B);
  and and_1 (and_1_out, A, B);
  and and_2 (and_2_out, xor_1_out, Cin);
  xor xor_2 (Sum, xor_1_out, Cin);
  or or_1 (Cout, and_2_out, and_1_out);

  // Notes on the sheet:
  //   Fixed I/O
  //   INPUTS
  //   Don't touch
  //   OUTPUTS
endmodule
