// Logisim project ex2.circ as structural Verilog: 2 circuits, main circuit Adder1
module Adder1 (
  input  [3:0] A,
  input  [3:0] B,
  output [3:0] Sum
);

  wire and_1_out, and_2_out, and_3_out, and_4_out, and_5_out, or_1_out, or_2_out, xor_1_out, xor_2_out,
       xor_3_out;

  and and_1 (and_1_out, A[0], B[0]);
  and and_2 (and_2_out, A[1], B[1]);
  and and_3 (and_3_out, A[2], B[2]);
  xor xor_1 (xor_1_out, A[1], B[1]);
  xor xor_2 (xor_2_out, A[2], B[2]);
  xor xor_3 (xor_3_out, A[3], B[3]);
  xor xor_4 (Sum[0], A[0], B[0]);
  xor xor_5 (Sum[1], and_1_out, xor_1_out);
  and and_4 (and_4_out, and_1_out, xor_1_out);
  or or_1 (or_1_out, and_4_out, and_2_out);
  xor xor_6 (Sum[2], or_1_out, xor_2_out);
  and and_5 (and_5_out, or_1_out, xor_2_out);
  or or_2 (or_2_out, and_5_out, and_3_out);
  xor xor_7 (Sum[3], or_2_out, xor_3_out);

  // Notes on the sheet:
  //   Fixed I/O
  //   INPUTS
  //   Don't touch
  //   OUTPUTS
endmodule

module Subtractor1 (
  input  [3:0] A,
  input  [3:0] B,
  output [3:0] Sum
);

  wire and_1_out, and_2_out, and_3_out, and_4_out, and_5_out, and_6_out, not_1_out, not_2_out, not_3_out,
       not_4_out, or_1_out, or_2_out, or_3_out, xor_1_out, xor_2_out, xor_3_out, xor_4_out;

  not not_1 (not_1_out, B[0]);
  not not_2 (not_2_out, B[1]);
  not not_3 (not_3_out, B[2]);
  not not_4 (not_4_out, B[3]);
  and and_1 (and_1_out, not_1_out, A[0]);
  and and_2 (and_2_out, A[1], not_2_out);
  and and_3 (and_3_out, A[2], not_3_out);
  xor xor_1 (xor_1_out, A[0], not_1_out);
  xor xor_2 (xor_2_out, A[1], not_2_out);
  xor xor_3 (xor_3_out, A[2], not_3_out);
  xor xor_4 (xor_4_out, A[3], not_4_out);
  and and_4 (and_4_out, 1'b1, xor_1_out);
  or or_1 (or_1_out, and_1_out, and_4_out);
  xor xor_5 (Sum[0], 1'b1, xor_1_out);
  and and_5 (and_5_out, or_1_out, xor_2_out);
  xor xor_6 (Sum[1], or_1_out, xor_2_out);
  or or_2 (or_2_out, and_5_out, and_2_out);
  xor xor_7 (Sum[2], or_2_out, xor_3_out);
  and and_6 (and_6_out, or_2_out, xor_3_out);
  or or_3 (or_3_out, and_6_out, and_3_out);
  xor xor_8 (Sum[3], or_3_out, xor_4_out);

  // Notes on the sheet:
  //   Fixed I/O
  //   INPUTS
  //   Don't touch
  //   OUTPUTS
endmodule
