// Logisim project ex3.circ as structural Verilog: 1 circuit, main circuit display_driver
module display_driver (
  input  [3:0] Input_Number,
  output [6:0] Disp
);

  wire and_1_out, and_2_out, and_3_out, and_4_out, and_5_out, and_6_out, and_7_out, and_8_out, and_9_out,
       and_10_out, and_11_out, and_12_out, and_13_out, and_14_out, and_15_out, and_16_out, and_17_out,
       and_18_out, and_19_out, and_20_out, and_21_out, and_22_out, and_23_out, and_24_out, and_25_out,
       and_26_out, and_27_out, and_28_out, and_29_out, and_30_out, and_31_out, and_32_out, and_33_out,
       and_34_out, not_1_out, not_2_out, not_3_out, not_4_out, not_5_out, not_6_out, not_7_out, not_8_out,
       not_9_out, not_10_out, not_11_out, not_12_out, not_13_out, not_14_out, not_15_out, not_16_out,
       not_17_out, not_18_out, not_19_out, not_20_out, not_21_out, not_22_out, not_23_out, not_24_out,
       not_25_out, not_26_out, not_27_out, not_28_out, xor_1_out;

  not not_1 (not_1_out, Input_Number[3]);
  not not_2 (not_2_out, Input_Number[3]);
  not not_3 (not_3_out, Input_Number[2]);
  not not_4 (not_4_out, Input_Number[2]);
  not not_5 (not_5_out, Input_Number[1]);
  not not_6 (not_6_out, Input_Number[0]);
  not not_7 (not_7_out, Input_Number[1]);
  not not_8 (not_8_out, Input_Number[0]);
  and and_1 (and_1_out, Input_Number[3], not_3_out);
  and and_2 (and_2_out, Input_Number[1], not_6_out);
  and and_3 (and_3_out, Input_Number[3], Input_Number[0]);
  and and_4 (and_4_out, not_1_out, Input_Number[2], not_5_out);
  and and_5 (and_5_out, not_3_out, Input_Number[1]);
  and and_6 (and_6_out, not_7_out, not_8_out);
  and and_7 (and_7_out, Input_Number[3], not_4_out);
  and and_8 (and_8_out, Input_Number[2], not_8_out);
  and and_9 (and_9_out, Input_Number[3], Input_Number[1]);
  and and_10 (and_10_out, not_2_out, Input_Number[2], not_7_out);
  or or_1 (Disp[0], and_1_out, and_2_out, and_3_out, and_4_out, and_5_out);
  or or_2 (Disp[1], and_6_out, and_7_out, and_8_out, and_9_out, and_10_out);
  not not_9 (not_9_out, Input_Number[3]);
  not not_10 (not_10_out, Input_Number[3]);
  not not_11 (not_11_out, Input_Number[2]);
  not not_12 (not_12_out, Input_Number[2]);
  not not_13 (not_13_out, Input_Number[1]);
  not not_14 (not_14_out, Input_Number[1]);
  not not_15 (not_15_out, Input_Number[0]);
  not not_16 (not_16_out, Input_Number[0]);
  _7_Segment_Display u_7_segment_display_1 (
    .g(Disp[0]), .f(Disp[1]), .a(Disp[2]), .b(Disp[3]), .e(Disp[4]), .d(Disp[5]), .c(Disp[6]));  // open: dp
  and and_11 (and_11_out, not_11_out, not_15_out);
  and and_12 (and_12_out, Input_Number[2], Input_Number[1]);
  and and_13 (and_13_out, not_9_out, Input_Number[1]);
  and and_14 (and_14_out, Input_Number[3], not_15_out);
  and and_15 (and_15_out, not_9_out, Input_Number[2], Input_Number[0]);
  and and_16 (and_16_out, Input_Number[1], not_15_out);
  and and_17 (and_17_out, Input_Number[3], not_11_out, not_13_out);
  and and_18 (and_18_out, not_12_out, not_14_out);
  and and_19 (and_19_out, not_12_out, not_16_out);
  and and_20 (and_20_out, not_10_out, not_14_out, not_16_out);
  and and_21 (and_21_out, not_10_out, Input_Number[1], Input_Number[0]);
  and and_22 (and_22_out, Input_Number[3], not_14_out, Input_Number[0]);
  or or_3 (Disp[2], and_11_out, and_12_out, and_13_out, and_14_out, and_15_out, and_16_out, and_17_out);
  or or_4 (Disp[3], and_18_out, and_19_out, and_20_out, and_21_out, and_22_out);
  not not_17 (not_17_out, Input_Number[3]);
  not not_18 (not_18_out, Input_Number[3]);
  not not_19 (not_19_out, Input_Number[2]);
  not not_20 (not_20_out, Input_Number[2]);
  not not_21 (not_21_out, Input_Number[1]);
  not not_22 (not_22_out, Input_Number[1]);
  not not_23 (not_23_out, Input_Number[0]);
  not not_24 (not_24_out, Input_Number[0]);
  and and_23 (and_23_out, Input_Number[1], not_23_out);
  and and_24 (and_24_out, Input_Number[3], Input_Number[2]);
  and and_25 (and_25_out, Input_Number[3], Input_Number[1]);
  and and_26 (and_26_out, not_19_out, not_23_out);
  and and_27 (and_27_out, Input_Number[3], not_22_out);
  and and_28 (and_28_out, not_20_out, Input_Number[1], Input_Number[0]);
  and and_29 (and_29_out, Input_Number[2], not_22_out, Input_Number[0]);
  and and_30 (and_30_out, not_18_out, not_20_out, not_24_out);
  and and_31 (and_31_out, Input_Number[2], Input_Number[1], not_24_out);
  or or_5 (Disp[4], and_23_out, and_24_out, and_25_out, and_26_out);
  or or_6 (Disp[5], and_27_out, and_28_out, and_29_out, and_30_out, and_31_out);
  not not_25 (not_25_out, Input_Number[3]);
  not not_26 (not_26_out, Input_Number[2]);
  not not_27 (not_27_out, Input_Number[1]);
  not not_28 (not_28_out, Input_Number[0]);
  xor xor_1 (xor_1_out, Input_Number[3], Input_Number[2]);
  and and_32 (and_32_out, not_27_out, Input_Number[0]);
  and and_33 (and_33_out, not_25_out, not_27_out);
  and and_34 (and_34_out, not_25_out, Input_Number[0]);
  or or_7 (Disp[6], xor_1_out, and_32_out, and_33_out, and_34_out);

  // Other names for the same wires on the sheet: Disp1 = Disp[0]; Disp2 = Disp[1]; Disp3 = Disp[2]; Disp4 = Disp[3];
  //   Disp5 = Disp[4]; Disp6 = Disp[5]; Disp7 = Disp[6]; D = Input_Number[0]; C = Input_Number[1];
  //   B = Input_Number[2]; A = Input_Number[3]

  // Notes on the sheet:
  //   Fixed I/O
  //   INPUTS
  //   Don't touch
  //   OUTPUTS
endmodule
