// Logisim project ex1.circ as structural Verilog: 1 circuit, main circuit Multiplier1
module Multiplier1 (
  input  [3:0] A,
  input  [3:0] B,
  output [7:0] result
);

  wire adder_1_cout, adder_2_cout, adder_2_out, adder_3_cout, adder_3_out, adder_4_cout, adder_4_out,
       adder_5_cout, adder_6_cout, adder_6_out, adder_7_cout, adder_7_out, adder_8_cout, adder_8_out,
       adder_9_cout, adder_10_cout, adder_11_cout, and_2_out, and_3_out, and_4_out, and_5_out, and_6_out,
       and_7_out, and_8_out, and_9_out, and_10_out, and_11_out, and_12_out, and_13_out, and_14_out,
       and_15_out, and_16_out;

  and and_1 (result[0], B[0], A[0]);
  and and_2 (and_2_out, B[0], A[1]);
  and and_3 (and_3_out, B[0], A[2]);
  and and_4 (and_4_out, B[0], A[3]);
  and and_5 (and_5_out, B[1], A[0]);
  and and_6 (and_6_out, B[1], A[1]);
  and and_7 (and_7_out, B[1], A[2]);
  and and_8 (and_8_out, B[1], A[3]);
  Adder #(.width(1)) adder_1 (.a(and_5_out), .b(and_2_out), .out(result[1]), .cin(1'b0), .cout(adder_1_cout));
  Adder #(.width(1)) adder_2 (.a(and_6_out), .b(and_3_out), .out(adder_2_out), .cin(adder_1_cout), .cout(adder_2_cout));
  Adder #(.width(1)) adder_3 (.a(and_7_out), .b(and_4_out), .out(adder_3_out), .cin(adder_2_cout), .cout(adder_3_cout));
  Adder #(.width(1)) adder_4 (.a(1'b0), .b(and_8_out), .out(adder_4_out), .cin(adder_3_cout), .cout(adder_4_cout));
  and and_9 (and_9_out, B[2], A[0]);
  and and_10 (and_10_out, B[2], A[1]);
  and and_11 (and_11_out, B[2], A[2]);
  and and_12 (and_12_out, B[2], A[3]);
  Adder #(.width(1)) adder_5 (.a(and_9_out), .b(adder_2_out), .out(result[2]), .cin(1'b0), .cout(adder_5_cout));
  Adder #(.width(1)) adder_6 (
    .a(and_10_out), .b(adder_3_out), .out(adder_6_out), .cin(adder_5_cout), .cout(adder_6_cout));
  Adder #(.width(1)) adder_7 (
    .a(and_11_out), .b(adder_4_out), .out(adder_7_out), .cin(adder_6_cout), .cout(adder_7_cout));
  Adder #(.width(1)) adder_8 (
    .a(and_12_out), .b(adder_4_cout), .out(adder_8_out), .cin(adder_7_cout), .cout(adder_8_cout));
  and and_13 (and_13_out, B[3], A[0]);
  and and_14 (and_14_out, B[3], A[1]);
  and and_15 (and_15_out, B[3], A[2]);
  and and_16 (and_16_out, B[3], A[3]);
  Adder #(.width(1)) adder_9 (.a(and_13_out), .b(adder_6_out), .out(result[3]), .cin(1'b0), .cout(adder_9_cout));
  Adder #(.width(1)) adder_10 (
    .a(and_14_out), .b(adder_7_out), .out(result[4]), .cin(adder_9_cout), .cout(adder_10_cout));
  Adder #(.width(1)) adder_11 (
    .a(and_15_out), .b(adder_8_out), .out(result[5]), .cin(adder_10_cout), .cout(adder_11_cout));
  Adder #(.width(1)) adder_12 (
    .a(and_16_out), .b(adder_8_cout), .out(result[6]), .cin(adder_11_cout), .cout(result[7]));

  // Other names for the same wires on the sheet: R0 = result[0]; R1 = result[1]; R2 = result[2]; R3 = result[3];
  //   R4 = result[4]; R5 = result[5]; R6 = result[6]; R7 = result[7]

  // Notes on the sheet:
  //   Fixed I/O
  //   INPUTS
  //   Don't touch
  //   OUTPUTS
endmodule
