// Logisim project ex2.circ as structural Verilog: 1 circuit, main circuit ALU
module ALU (
  input  [3:0] A,
  input  [3:0] B,
  input  [2:0] ALU_sel,
  output [3:0] result
);

  wire [0:0] comparator_1_gt;
  wire [3:0] adder_1_out, and_1_out, shifter_1_out, shifter_2_out, subtractor_1_out;
  wire [7:0] multiplier1_1_result;

  Adder #(.width(4)) adder_1 (.a(A), .b(B), .out(adder_1_out));  // open: cin, cout
  Subtractor #(.width(4)) subtractor_1 (.a(A), .b(B), .out(subtractor_1_out));  // open: bin, bout
  Comparator #(.mode("unsigned"), .width(4)) comparator_1 (.a(A), .b(B), .gt(comparator_1_gt[0]));  // open: eq, lt
  Shifter #(.width(4)) shifter_1 (.in(A), .\dist (2'b01), .out(shifter_1_out));
  Shifter #(.shift("lr"), .width(4)) shifter_2 (.in(A), .\dist (2'b01), .out(shifter_2_out));
  assign and_1_out = A & B;  // AND_Gate and_1, 4 bits wide
  Multiplier1 multiplier1_1 (.A(A), .B(B), .result(multiplier1_1_result));
  Multiplexer #(.select(3), .width(4)) multiplexer_1 (
    .in0(adder_1_out), .in1(subtractor_1_out), .in2(multiplier1_1_result[3:0]),
    .in3(multiplier1_1_result[7:4]), .in4({3'b000, comparator_1_gt[0]}), .in5(shifter_1_out),
    .in6(shifter_2_out), .in7(and_1_out), .out(result), .sel(ALU_sel));

  // Notes on the sheet:
  //   Fixed I/O
  //   INPUTS
  //   Don't touch
  //   OUTPUTS
endmodule
